# Fritzing sketch hall-pyörintäanturi (saved by Fritzing 0.8.5b)
stripboards: 1

parts:
  HALL1 = TLE49x5L HALL Effect Sensor [package=PG-SSO-3-2]
  HALL2 = TLE49x5L HALL Effect Sensor [package=PG-SSO-3-2]
  J1_(r1_Vin_r2_GND_r3_H1q_r3_H2q) = male pin header, 4 pins [form="♂ (male)"]
  R1 = Resistor [tolerance=±5% resistance=1.5k package=THT]
  R2 = Resistor [tolerance=±5% resistance=1.5k package=THT]

nets:
  N1: HALL1.+Vs, HALL2.+Vs, J1_(r1_Vin_r2_GND_r3_H1q_r3_H2q).pin1, R1.Pin_0, R2.Pin_0
  GND: HALL1.GND, HALL2.GND, J1_(r1_Vin_r2_GND_r3_H1q_r3_H2q).pin2
  N2: HALL1.Q, J1_(r1_Vin_r2_GND_r3_H1q_r3_H2q).pin3, R1.Pin_1
  N3: HALL2.Q, J1_(r1_Vin_r2_GND_r3_H1q_r3_H2q).pin4, R2.Pin_1

custom parts:
  TLE49x5L HALL Effect Sensor: Uni- and Bipolar Hall IC Switch for Magnetic Field Applications
