# Fritzing sketch hc-05-bluetooth-johtosarja (saved by Fritzing 0.8.5b)

parts:
  HC-1 = HC-05 Bluetooth serial module
  R2 = Resistor [tolerance=±1% resistance=3.3k package=THT]
  R1 = Resistor [tolerance=±1% resistance=1.5k package=THT]
  r1_GND;_r2_+5V = female pin header, 2 pins [form="♀ (female)"]
  r1_TX;_r2_RX = female pin header, 2 pins [form="♀ (female)"]

nets:
  N1: HC-1.RX_3.3V, R2.Pin_0, R1.Pin_0
  N2: HC-1.TX, r1_TX;_r2_RX.pin2
  N3: HC-1.VCC, r1_GND;_r2_+5V.pin2
  N4: HC-1.GND, R2.Pin_1, r1_GND;_r2_+5V.pin1
  N5: R1.Pin_1, r1_TX;_r2_RX.pin1

custom parts:
  HC-05 Bluetooth serial module: These modems work as a serial (RX/TX) pipe, and are a great wireless replacement for serial cables. Any serial stream from 9600 to 115200bps can be passed seamlessly from your computer to your target. Bluetooth Mate has the same pin out as the FTDI Basic, and is meant to plug directly into an Arduino Pro, Pro Mini, or LilyPad Mainboard. Because we've arranged the pins to do this, you cannot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
