# Fritzing sketch johtosarja-pfet-versio2 (saved by Fritzing 0.8.5b)
circuit board: 1.8134cm x 6.66955cm
stripboards: 1

parts:
  Part1 = Arduino Nano (Rev3.0)  # not connected
  r1_GND_r2_BAT_+_r3_SERVO_POWER_CONTROL_PIN_r4_SERVO_POSITION_ANALOGREAD_PIN1 = male pin header, 4 pins [form="♂ (male)"]
  r1_GND_r2_BAT_+_r3_HALL_INT0_r4_HALL_SENSOR_2_PIN_(7) = male pin header, 4 pins [form="♂ (male)"]
  r1_GND_r2_BTN_+5V_r3_BTN_ANALOGREAD_PIN1_r4_RESERVED = male pin header, 4 pins [form="♂ (male)"]
  J4 = rounded female pin header, 15 pins [form="♀ (female rounded)"]
  J5 = rounded female pin header, 15 pins [form="♀ (female rounded)"]
  BT_-_r1_GND;_r2_BAT_+ = male pin header, 2 pins [form="♂ (male)"]
  BT_-_r1_TX;_r2_RX = male pin header, 2 pins [form="♂ (male)"]
  R3 = Resistor [tolerance=±5% resistance=2.2k package=THT]
  R2 = Resistor [tolerance=±5% resistance=10k part_number="pull-up, prevent gate floating & random triggering" package=THT]
  Power_-_r1_GND;_r2_BAT_+1 = male pin header, 2 pins [form="♂ (male)"]
  D3 = Rectifier Diode [part_number=1N4001 package="300 mil [THT]"]
  Q1 = MOSFET-PCHANNEL [part_number=BS250 package=to-92]

nets:
  N1: r1_GND_r2_BAT_+_r3_SERVO_POWER_CONTROL_PIN_r4_SERVO_POSITION_ANALOGREAD_PIN1.pin1, r1_GND_r2_BAT_+_r3_HALL_INT0_r4_HALL_SENSOR_2_PIN_(7).pin1, r1_GND_r2_BTN_+5V_r3_BTN_ANALOGREAD_PIN1_r4_RESERVED.pin1, J4.pin4, J5.pin2, BT_-_r1_GND;_r2_BAT_+.pin1, Power_-_r1_GND;_r2_BAT_+1.pin2, D3.anode
  N2: r1_GND_r2_BAT_+_r3_SERVO_POWER_CONTROL_PIN_r4_SERVO_POSITION_ANALOGREAD_PIN1.pin2, D3.cathode, Q1.D
  N3: r1_GND_r2_BAT_+_r3_SERVO_POWER_CONTROL_PIN_r4_SERVO_POSITION_ANALOGREAD_PIN1.pin3, J4.pin9
  N4: r1_GND_r2_BAT_+_r3_SERVO_POWER_CONTROL_PIN_r4_SERVO_POSITION_ANALOGREAD_PIN1.pin4, J5.pin5
  N5: r1_GND_r2_BAT_+_r3_HALL_INT0_r4_HALL_SENSOR_2_PIN_(7).pin2, r1_GND_r2_BTN_+5V_r3_BTN_ANALOGREAD_PIN1_r4_RESERVED.pin2, J5.pin4, BT_-_r1_GND;_r2_BAT_+.pin2
  N6: r1_GND_r2_BAT_+_r3_HALL_INT0_r4_HALL_SENSOR_2_PIN_(7).pin3, J4.pin5
  N7: r1_GND_r2_BAT_+_r3_HALL_INT0_r4_HALL_SENSOR_2_PIN_(7).pin4, J4.pin10
  N8: r1_GND_r2_BTN_+5V_r3_BTN_ANALOGREAD_PIN1_r4_RESERVED.pin3, J5.pin6
  N9: J4.pin1, BT_-_r1_TX;_r2_RX.pin1
  N10: J4.pin2, BT_-_r1_TX;_r2_RX.pin2
  N11: J4.pin8, R3.Pin_1
  N12: J5.pin1, R2.Pin_0, Power_-_r1_GND;_r2_BAT_+1.pin1, Q1.S
  N13: R3.Pin_0, R2.Pin_1, Q1.G

notes:
  TODO:
  - bluetooth virtakytkin?

custom parts:
  MOSFET-PCHANNEL: BS250 P-channel mosfet, huom, schema väärin!
