# Fritzing sketch vaihdepainikkeet (saved by Fritzing 0.8.5b)
perfboards: 1
stripboards: 1

parts:
  btn_Up = Pushbutton [package=THT]
  R11 = Resistor [tolerance=±5% resistance=22k package=THT]
  R12 = Resistor [tolerance=±5% resistance=10k package=THT]
  R13 = Resistor [tolerance=±5% resistance=22k package=THT]
  R14 = Resistor [tolerance=±5% resistance=22k package=THT]
  btn_Down = Pushbutton [package=THT]
  Blue_#4_-_Black_GND_-_Red_+5v = Header 3 [package=molex-1x3_lock]
  Blue_B1_-_Black_GND_-_Red_B2 = Header 3 [package=molex-1x3_lock]
  btn_Up1 = Pushbutton [package=THT]
  btn_Down1 = Pushbutton [package=THT]

nets:
  N1: btn_Up.leg0, R11.Pin_0
  N2: btn_Up.leg1, btn_Down.leg1, Blue_#4_-_Black_GND_-_Red_+5v.3
  N3: R11.Pin_1, R12.Pin_0, R13.Pin_1
  N4: R12.Pin_1, R14.Pin_1, Blue_#4_-_Black_GND_-_Red_+5v.1
  N5: R13.Pin_0, Blue_#4_-_Black_GND_-_Red_+5v.2
  N6: R14.Pin_0, btn_Down.leg0
  N7: Blue_B1_-_Black_GND_-_Red_B2.1, btn_Up1.leg1
  N8: Blue_B1_-_Black_GND_-_Red_B2.2, btn_Up1.leg0, btn_Down1.leg0
  N9: Blue_B1_-_Black_GND_-_Red_B2.3, btn_Down1.leg1

notes:
  Analog version: to speed things up, try lowering resistor values to lower the impendance towards Arduino's ADC
